// Logisim project full-adder.circ as structural Verilog: 1 circuit, main circuit main
module main (
  input  switch_A,
  input  switch_B,
  input  switch_C,
  output Sum,
  output Carry
);

  wire and_1_out, and_2_out, xor_1_out;

  xor xor_1 (xor_1_out, switch_A, switch_B);
  and and_1 (and_1_out, switch_B, switch_A);
  xor xor_2 (Sum, xor_1_out, switch_C);
  and and_2 (and_2_out, switch_C, xor_1_out);
  or or_1 (Carry, and_2_out, and_1_out);

  // Notes on the sheet:
  //   Full Adder
endmodule
