// Logisim project full-subtracter.circ as structural Verilog: 1 circuit, main circuit main
module main (
  input  switch_A,
  input  switch_B,
  input  switch_C,
  output Difference,
  output Borrow
);

  wire and_1_out, and_2_out, not_1_out, not_2_out, xor_1_out;

  not not_1 (not_1_out, switch_A);
  xor xor_1 (xor_1_out, switch_A, switch_B);
  and and_1 (and_1_out, switch_B, not_1_out);
  xor xor_2 (Difference, xor_1_out, switch_C);
  and and_2 (and_2_out, switch_C, not_2_out);
  not not_2 (not_2_out, xor_1_out);
  or or_1 (Borrow, and_2_out, and_1_out);

  // Notes on the sheet:
  //   Full Subtracter
endmodule
