// Logisim project half-adder.circ as structural Verilog: 1 circuit, main circuit main
module main (
  input  switch_a,
  input  switch_b,
  output sum,
  output carry
);

  xor xor_1 (sum, switch_a, switch_b);
  and and_1 (carry, switch_a, switch_b);

  // Notes on the sheet:
  //   Half Adder
endmodule
