// Logisim project half-subtracter.circ as structural Verilog: 1 circuit, main circuit main
module main (
  input  switch_A,
  input  switch_B,
  output Difference,
  output Borrow
);

  wire not_1_out;

  not not_1 (not_1_out, switch_A);
  xor xor_1 (Difference, switch_A, switch_B);
  and and_1 (Borrow, switch_B, not_1_out);

  // Notes on the sheet:
  //   Half Subtracter
endmodule
