// Logisim project 1-4-2-encoder.circ as structural Verilog: 1 circuit, main circuit main
module main (
  input  i0,
  input  i1,
  input  i2,
  input  i3,
  output [1:0] Output
);

  Priority_Encoder #(.select(2)) priority_encoder_1 (
    .in0(i0), .in1(i1), .in2(i2), .in3(i3), .out(Output));  // open: gs, en_out, en_in

  // Notes on the sheet:
  //   1. Design a circuit for 4-2 encoder.
endmodule
