// Logisim project 2-3-8-decoder.circ as structural Verilog: 1 circuit, main circuit main
module main (
  input  [2:0] in_1,
  output o0,
  output o1,
  output _02,
  output _03,
  output _04,
  output _05,
  output _06,
  output _07
);

  Decoder #(.select(3)) decoder_1 (
    .out0(o0), .out1(o1), .out2(_02), .out3(_03), .out4(_04), .out5(_05), .out6(_06), .out7(_07), .sel(in_1));  // open: en

  // Notes on the sheet:
  //   2. Design 3 to 8 Decoder.
endmodule
