// Logisim project 4-alu.circ as structural Verilog: 1 circuit, main circuit main
module main (
  input  [7:0] in_1,
  input  [7:0] in_2,
  input  [7:0] in_3,
  input  [2:0] in_4,
  input  [2:0] in_5,
  input  [2:0] in_6,
  output [7:0] out_7
);

  wire [7:0] adder_1_out, divider_1_out, multiplier_1_out, negator_1_out, shifter_1_out, shifter_2_out,
       subtractor_1_out;

  Adder adder_1 (.a(in_1), .b(in_3), .out(adder_1_out));  // open: cin, cout
  Subtractor subtractor_1 (.a(in_1), .b(in_3), .out(subtractor_1_out));  // open: bin, bout
  Multiplier multiplier_1 (.a(in_1), .b(in_3), .out(multiplier_1_out));  // open: cin, cout
  Divider divider_1 (.a(in_1), .b(in_3), .out(divider_1_out));  // open: upper, rem
  Negator negator_1 (.in(in_1), .out(negator_1_out));
  Shifter shifter_1 (.in(in_1), .\dist (in_5), .out(shifter_1_out));
  Shifter #(.shift("lr")) shifter_2 (.in(in_1), .\dist (in_6), .out(shifter_2_out));
  Multiplexer #(.select(3), .width(8), .enable("false")) multiplexer_1 (
    .in0(adder_1_out), .in1(subtractor_1_out), .in2(multiplier_1_out), .in3(divider_1_out),
    .in4(negator_1_out), .in5(shifter_1_out), .in6(shifter_2_out), .in7(in_2), .out(out_7), .sel(in_4));
endmodule
