// Logisim project 5-and.circ as structural Verilog: 1 circuit, main circuit main
module main (
  input  a,
  input  b,
  input  c,
  input  d,
  input  e,
  input  f,
  input  g,
  input  h,
  output x,
  output y,
  output z,
  output u
);

  and and_1 (x, a, e);
  and and_2 (y, b, f);
  and and_3 (z, c, g);
  and and_4 (u, d, h);
endmodule
