// Logisim project 7-1x4-demux.circ as structural Verilog: 1 circuit, main circuit main
module main (
  input  Input,
  input  S1,
  input  S2,
  output O1,
  output O2,
  output O3,
  output O4
);

  wire not_1_out, not_2_out;

  not not_1 (not_1_out, S1);
  not not_2 (not_2_out, S2);
  and and_1 (O1, S1, S2, Input);
  and and_2 (O2, S1, not_2_out, Input);
  and and_3 (O3, not_1_out, S2, Input);
  and and_4 (O4, not_1_out, not_2_out, Input);

  // Notes on the sheet:
  //   7. Design a cicuit for 1:4 DeMultiplexer using gates.
endmodule
