// Logisim project 8-4x1.circ as structural Verilog: 1 circuit, main circuit main
module main (
  input  S1,
  input  S0,
  input  switch_A,
  input  switch_B,
  input  switch_C,
  output out_6
);

  wire and_1_out, and_2_out, and_3_out, and_4_out, and_5_out, and_6_out, and_7_out, and_8_out, not_1_out,
       not_2_out, not_3_out, or_1_out, or_2_out, xnor_1_out, xnor_2_out, xor_1_out, xor_2_out;

  and and_1 (and_1_out, switch_B, switch_A);
  and and_2 (and_2_out, switch_A, not_1_out);
  not not_1 (not_1_out, switch_A);
  xor xor_1 (xor_1_out, switch_A, switch_B);
  xnor xnor_1 (xnor_1_out, switch_A, switch_A);
  xor xor_2 (xor_2_out, xor_1_out, switch_C);
  and and_3 (and_3_out, switch_C, xor_1_out);
  xnor xnor_2 (xnor_2_out, xnor_1_out, switch_C);
  and and_4 (and_4_out, switch_C, xnor_1_out);
  or or_1 (or_1_out, and_3_out, and_1_out);
  or or_2 (or_2_out, and_4_out, and_2_out);
  not not_2 (not_2_out, S1);
  not not_3 (not_3_out, S0);
  and and_5 (and_5_out, xor_2_out, not_2_out, not_3_out);
  and and_6 (and_6_out, xnor_2_out, not_2_out, S0);
  and and_7 (and_7_out, or_1_out, S1, not_3_out);
  and and_8 (and_8_out, or_2_out, S1, S0);
  or or_3 (out_6, and_5_out, and_6_out, and_7_out, and_8_out);
endmodule
