// Logisim project divider.circ as structural Verilog: 1 circuit, main circuit main
module main (
  input  [3:0] in_1,
  input  [3:0] in_2,
  output [3:0] out_3
);

  Divider #(.width(4)) divider_1 (.a(in_1), .b(in_2), .out(out_3));  // open: upper, rem
endmodule
