// Logisim project q1.circ as structural Verilog: 1 circuit, main circuit main
module main (
  input  [7:0] Write_Data,
  input  Write,
  input  [7:0] Address,
  input  in_4,
  input  [7:0] Address_2,
  output [7:0] out_6,
  output [7:0] out_7
);

  wire not_1_out;

  assign out_6 = Write ? Write_Data : 8'bz;  // Controlled_Buffer controlled_buffer_1
  not not_1 (not_1_out, Write);
  RAM ram_1 (.addr(Address), .data(out_6), .clk(in_4), .ld(not_1_out));  // open: sel, clr
  ROM rom_1 (.addr(Address_2), .data(out_7));  // open: sel

  // Notes on the sheet:
  //   contents of rom_1 (hex, n*v repeats v):
  //   6 0 0 1 0 0 0 f
endmodule
