// Logisim project q2.circ as structural Verilog: 1 circuit, main circuit main
module main (
  input  in_1,
  input  in_2,
  output [2:0] out_3
);

  wire clock_1_out;
  wire [7:0] rom_1_data;

  ROM #(.addrWidth(3)) rom_1 (.addr(out_3), .data(rom_1_data));  // open: sel
  Clock clock_1 (.out(clock_1_out));
  Counter #(.width(3), .max('h7)) counter_1 (.count(in_2), .Q(out_3), .clk(clock_1_out));  // open: load, D, carry, clr
  RAM #(.addrWidth(3)) ram_1 (.addr(out_3), .data(rom_1_data), .clk(clock_1_out), .ld(in_1));  // open: sel, clr

  // Notes on the sheet:
  //   contents of rom_1 (hex, n*v repeats v):
  //   0 1 2 3 4 5 6 7
endmodule
