// Logisim project q3.circ as structural Verilog: 1 circuit, main circuit main
module main (
  input  B0,
  input  B1,
  input  A1,
  input  A0,
  input  in_5,
  input  in_6,
  output P1,
  output out_8,
  output out_9,
  output out_10
);

  wire and_1_out, and_2_out, and_3_out, and_4_out, and_5_out, and_6_out, and_8_out, or_1_out, xor_1_out,
       xor_2_out;

  xor xor_1 (xor_1_out, and_8_out, and_6_out);
  xor xor_2 (xor_2_out, and_5_out, or_1_out);
  and and_1 (and_1_out, and_8_out, and_6_out);
  and and_2 (and_2_out, and_5_out, or_1_out);
  and and_3 (and_3_out, in_5, xor_1_out);
  and and_4 (and_4_out, in_6, xor_2_out);
  and and_5 (and_5_out, A1, B1);
  xor xor_3 (P1, xor_1_out, in_5);
  xor xor_4 (out_10, xor_2_out, in_6);
  and and_6 (and_6_out, A0, B1);
  or or_1 (or_1_out, and_3_out, and_1_out);
  or or_2 (out_9, and_4_out, and_2_out);
  and and_7 (out_8, A0, B0);
  and and_8 (and_8_out, A1, B0);

  // Notes on the sheet:
  //   2-BIT MULTIPLIER
  //   P3
  //   P0
  //   P2
endmodule
