// Logisim project q1.circ as structural Verilog: 1 circuit, main circuit main
module main (
  input  [7:0] in_1,
  input  in_2
);

  wire and_1_out, and_2_out, and_3_out, and_4_out, clock_1_out, not_1_out, not_2_out, not_3_out, not_4_out,
       not_5_out, not_6_out, not_7_out, not_8_out, or_1_out, or_2_out, or_3_out, or_4_out, or_5_out,
       or_6_out, or_7_out, or_8_out;
  wire [7:0] register_1_q;

  not not_1 (not_1_out, register_1_q[7]);
  not not_2 (not_2_out, register_1_q[6]);
  Register register_1 (.D(in_1), .en(in_2), .Q(register_1_q), .clk(clock_1_out));  // open: clr
  Clock clock_1 (.out(clock_1_out));
  _7_Segment_Display u_7_segment_display_1 (
    .g(register_1_q[7]), .f(and_1_out), .a(or_2_out), .b(1'b1), .e(not_2_out), .d(or_2_out), .c(or_1_out));  // open: dp
  or or_1 (or_1_out, not_1_out, register_1_q[6]);
  and and_1 (and_1_out, not_1_out, not_2_out);
  or or_2 (or_2_out, not_2_out, register_1_q[7]);
  not not_3 (not_3_out, register_1_q[5]);
  not not_4 (not_4_out, register_1_q[4]);
  _7_Segment_Display u_7_segment_display_2 (
    .g(register_1_q[5]), .f(and_2_out), .a(or_4_out), .b(1'b1), .e(not_4_out), .d(or_4_out), .c(or_3_out));  // open: dp
  or or_3 (or_3_out, not_3_out, register_1_q[4]);
  and and_2 (and_2_out, not_3_out, not_4_out);
  or or_4 (or_4_out, not_4_out, register_1_q[5]);
  not not_5 (not_5_out, register_1_q[3]);
  not not_6 (not_6_out, register_1_q[2]);
  _7_Segment_Display u_7_segment_display_3 (
    .g(register_1_q[3]), .f(and_3_out), .a(or_6_out), .b(1'b1), .e(not_6_out), .d(or_6_out), .c(or_5_out));  // open: dp
  or or_5 (or_5_out, not_5_out, register_1_q[2]);
  and and_3 (and_3_out, not_5_out, not_6_out);
  or or_6 (or_6_out, not_6_out, register_1_q[3]);
  not not_7 (not_7_out, register_1_q[1]);
  not not_8 (not_8_out, register_1_q[0]);
  _7_Segment_Display u_7_segment_display_4 (
    .g(register_1_q[1]), .f(and_4_out), .a(or_8_out), .b(1'b1), .e(not_8_out), .d(or_8_out), .c(or_7_out));  // open: dp
  or or_7 (or_7_out, not_7_out, register_1_q[0]);
  and and_4 (and_4_out, not_7_out, not_8_out);
  or or_8 (or_8_out, not_8_out, register_1_q[1]);

  // Notes on the sheet:
  //   OPCODE
  //   OP1
  //   OP2
  //   OFFSET
endmodule
